# Fritzing sketch acceleration (saved by Fritzing 0.9.3b)
breadboards: 1

parts:
  パーツ1 = Arduino Uno (Rev3)
  U1 = ADXL193 [package=adxl193]
  U2 = microSD Socket [package="Molex 502774-0891 [SMD]"]  # not connected

nets:
  N1: パーツ1.A0, U1.OUT
  N2: パーツ1.A1, U1.VDD
  N3: パーツ1.A2, U1.VDD2
  GND: パーツ1.GND, U1.GND
